# Fritzing sketch GYRO (saved by Fritzing 0.9.3b)
breadboards: 1

parts:
  Capteur = InvenSense MPU6050
  Microcontrôleur = Arduino Nano (Rev3.0)
  J1 = Basic Servo
  J2 = Basic Servo
  VCC1 = Battery
  A1 = mini boost module

nets:
  VCC: Capteur.VCC, Microcontrôleur.5V, J1.vcc, J2.vcc, A1.Pin_4
  GND: Capteur.GND, Microcontrôleur.GND, J1.gnd, J2.gnd, A1.Pin_3
  N1: Capteur.SCL, Microcontrôleur.A5
  N2: Capteur.SDA, Microcontrôleur.A4
  N3: Microcontrôleur.D10, J1.pulse
  N4: Microcontrôleur.D11/MOSI, J2.pulse
  N5: VCC1.-, A1.Pin_1
  N6: VCC1.+, A1.Pin_2

custom parts:
  mini boost module: mini boost module.
